# Fritzing sketch Wiring Schematic (saved by Fritzing 0.9.10b)
breadboards: 1

parts:
  Arduino_UNO_R3 = Arduino Ethernet Shield (Rev3)
  Ultrasonic_Sensor = HC-SR04 Ultrasonic Distance Sensor
  Left_Motor = gear-motor
  Right_Motor = gear-motor
  IMU = InvenSense MPU6050
  part = L298N DC motor driver
  IR_Receiver = TSOP312.., 314.. [package=THT]
  Battery_Cell = Battery block 9V

nets:
  GND: Arduino_UNO_R3.GND, Ultrasonic_Sensor.GND, IMU.GND, part.GND, IR_Receiver.GND, Battery_Cell.-
  N1: Arduino_UNO_R3.D8, part.IN4
  N2: Arduino_UNO_R3.PWM_D9, part.ENA
  N3: Arduino_UNO_R3.PWM_D11, IR_Receiver.Data
  N4: Arduino_UNO_R3.SPI/D12, part.IN1
  N5: Arduino_UNO_R3.SPI/D13, part.IN2
  N6: Arduino_UNO_R3.A4/SDA, IMU.SDA
  N7: Arduino_UNO_R3.A5/SCL, IMU.SCL
  N8: Arduino_UNO_R3.SDCS, Ultrasonic_Sensor.TRIG
  N9: Arduino_UNO_R3.PWM_D5, Ultrasonic_Sensor.ECHO
  N10: Arduino_UNO_R3.PWM_D6, part.ENB
  N11: Arduino_UNO_R3.D7, part.IN3
  VCC: Arduino_UNO_R3.VIN, Ultrasonic_Sensor.VCC, IMU.VCC, part.5V, IR_Receiver.Vs
  N12: Left_Motor.pin_1, part.OUT3
  N13: Left_Motor.pin_2, part.OUT4
  N14: Right_Motor.pin_1, part.OUT1
  N15: Right_Motor.pin_2, part.OUT2
  N16: part.12V, Battery_Cell.+

custom parts:
  L298N DC motor driver: 2x DC motor driver with 78M05 positive voltage regulator (7..35 V) L298N: max 46 V, 2 A Set 5 V Enable jumper to enable 5 V regultor (needed for the L298N) and +5 V output at screw terminal or supply external +5 V at screw terminal Set ENA and/or ENB to +5 V to enable motor permanently or supply ENA and/or ENB with PWM signal IN1 and IN2 set rotation directory for motor A (OUT1/OUT2) IN2 and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
